# Fritzing sketch cablage-bras-robot (saved by Fritzing 1.0.6)
breadboards: 1

parts:
  M1 = ESP32-C3-DevKitC-02 [part_number=ESP32-C3-DevKitC-02]
  SERVO1 = Tower Pro SG90 servo [part_number=101246]
  SERVO2 = Tower Pro SG90 servo [part_number=101246]
  SERVO3 = Tower Pro SG90 servo [part_number=101246]  # not connected
  SERVO4 = Tower Pro SG90 servo [part_number=101246]  # not connected

nets:
  N1: M1.GND#0, M1.GND#1, M1.GND#7, M1.GND#9, M1.GND#14, M1.GND#15, M1.GND#19, M1.GND#24, M1.GND#29
  N2: M1.3, SERVO2.Signal
  N3: M1.9, SERVO1.Signal

custom parts:
  ESP32-C3-DevKitC-02: Esp32-C3 DevKitC 02 is one of the development board created by Espressif. It is based on the ESP32 microcontroller that boasts Wifi, Bluetooth, Ethernet and Low Power support all in a single chip. (vanepp) Feb 2021: converted to ESP32-C3-DevKitC-02. This chip is 30pins long (2 x15) and 11 pins width.
  Tower Pro SG90 servo: Original file by John De Cristofaro http://www.adafruit.com/products/1449 Adafruit Feedback Servo (Small) Edited by: e-radionica.com 28/9/2015
