# Fritzing sketch cablage-manette  (saved by Fritzing 1.0.6)
breadboards: 1

parts:
  U1 = ESP32-38PinWide [part_number=ESP32-38PinWide]
  Mod1 = KY-023 Dual Axis Joystick Module [package="Breakout board"]
  Mod2 = KY-023 Dual Axis Joystick Module [package="Breakout board"]
  VCC1 = Battery [internal_resistance=0.1Ω]

nets:
  N1: U1.GPIO34, Mod2.VRx
  N2: U1.GPIO35, Mod2.VRy
  N3: U1.GPIO32, Mod1.VRx
  N4: U1.GPIO33, Mod1.VRy
  N5: U1.GPIO25, Mod1.SW
  N6: U1.GPIO26, Mod2.SW
  N7: U1.GND, VCC1.-

custom parts:
  ESP32-38PinWide: Generic 38-Pin ESP32 with wide format (only access to one side of pins on a breadboard) based on Stephen Lilley's HiLetgo ESP-WROOM-32 ESP32 ESP-32S Development Board.
  KY-023 Dual Axis Joystick Module: KY-023 Dual-Axis Joystick Module.
